// Logisim project 1.1) Première utilisation d_un circuit intégré.circ as structural Verilog: 1 circuit, main circuit main
module main (
  input  in_1,
  input  in_2,
  output out_3
);

  nand nand_1 (out_3, in_1, in_2);
  LED led_1 (.in(out_3));
endmodule
